# Fritzing sketch stoplicht (saved by Fritzing 0.9.10b)
breadboards: 1

parts:
  M1 = ESP32-S2-DevKitC-1 [part_number=ESP32-S2-DevKitC-1]
  LED1 = LED - 5mm [color="Red (633nm)" current=0.030 package="5 mm [THT]"]
  R1 = Resistor [tolerance=±5% power=0.25 resistance=220 package=THT]
  R2 = Resistor [tolerance=±5% power=0.25 resistance=220 package=THT]
  R3 = Resistor [tolerance=±5% power=0.25 resistance=220 package=THT]
  LED2 = LED - 5mm [color="Yellow (595nm)" current=0.030 package="5 mm [THT]"]
  LED3 = LED - 5mm [color="Green (570nm)" current=0.030 package="5 mm [THT]"]
  S1 = Pushbutton [package="[THT]"]
  R4 = Resistor [tolerance=±5% power=0.25 resistance=220 package=THT]

nets:
  N1: M1.pin_1, M1.pin_2
  N2: M1.pin_22, M1.pin_23, M1.pin_24, M1.pin_44, R1.Pin_0, R2.Pin_0, R3.Pin_0, S1.Pin_3, S1.Pin_4, R4.Pin_0
  N3: M1.pin_29, S1.Pin_1, S1.Pin_2, R4.Pin_1
  N4: M1.pin_30, LED3.cathode
  N5: M1.pin_31, LED2.cathode
  N6: M1.pin_32, LED1.cathode
  N7: LED1.anode, R3.Pin_1
  N8: R1.Pin_1, LED3.anode
  N9: R2.Pin_1, LED2.anode

custom parts:
  ESP32-S2-DevKitC-1: ESP32-S2-DevKitC-1 is an entry-level development board based on ESP32-S2-SOLO (on-board PCB antenna). It is based on the ESP32 microcontroller that boasts Wifi, Bluetooth, Ethernet and Low Power support all in a single chip. (vanepp) Feb 2022: converted to ESP32-S2-DevKitC-1. This module is 44pins long (2x22) and 11 pins width.
