# Fritzing sketch pong_sketch (saved by Fritzing 0.9.10b)
breadboards: 4

parts:
  M1 = ESP32-S2-DevKitC-1 [part_number=ESP32-S2-DevKitC-1]
  D1 = LED_BARGRAPH_10 [package=led_bargaph_10]
  LED1 = 7-SEGMENT-4DIGIT-YOUNGSUN [package=7-segment-4digit-youngsun]
  S1 = Pushbutton [package="[THT]"]
  S2 = Pushbutton [package="[THT]"]
  R1 = Resistor [tolerance=±5% power=0.25 resistance=220 package=THT]
  R2 = Resistor [tolerance=±5% power=0.25 resistance=220 package=THT]
  R3 = Resistor [tolerance=±5% power=0.25 resistance=220 package=THT]
  R4 = Resistor [tolerance=±5% power=0.25 resistance=220 package=THT]
  R5 = Resistor [tolerance=±5% power=0.25 resistance=220 package=THT]
  R6 = Resistor [tolerance=±5% power=0.25 resistance=220 package=THT]
  R7 = Resistor [tolerance=±5% power=0.25 resistance=220 package=THT]
  R8 = Resistor [tolerance=±5% power=0.25 resistance=220 package=THT]
  R9 = Resistor [tolerance=±5% power=0.25 resistance=220 package=THT]
  R10 = Resistor [tolerance=±5% power=0.25 resistance=220 package=THT]
  R11 = Resistor [tolerance=±5% power=0.25 resistance=220 package=THT]
  R12 = Resistor [tolerance=±5% power=0.25 resistance=220 package=THT]
  R13 = Resistor [tolerance=±5% power=0.25 resistance=220 package=THT]
  R14 = Resistor [tolerance=±5% power=0.25 resistance=220 package=THT]
  R15 = Resistor [tolerance=±5% power=0.25 resistance=220 package=THT]
  R16 = Resistor [tolerance=±5% power=0.25 resistance=220 package=THT]
  R17 = Resistor [tolerance=±5% power=0.25 resistance=220 package=THT]
  R18 = Resistor [tolerance=±5% power=0.25 resistance=220 package=THT]
  R19 = Resistor [tolerance=±5% power=0.25 resistance=220 package=THT]
  R20 = Resistor [tolerance=±5% power=0.25 resistance=220 package=THT]

nets:
  N1: M1.pin_1, M1.pin_2, S1.Pin_3, S1.Pin_4, S2.Pin_3, S2.Pin_4
  N2: M1.pin_4, LED1.B, R13.Pin_0, R13.Pin_1
  N3: M1.pin_5, LED1.G, R14.Pin_0, R14.Pin_1
  N4: M1.pin_6, LED1.A, R15.Pin_0, R15.Pin_1
  N5: M1.pin_7, LED1.C, R16.Pin_0, R16.Pin_1
  N6: M1.pin_8, LED1.COL-C, R17.Pin_0, R17.Pin_1
  N7: M1.pin_9, LED1.F, R18.Pin_0, R18.Pin_1
  N8: M1.pin_10, LED1.APOS-A, R19.Pin_0, R19.Pin_1
  N9: M1.pin_11, LED1.APOS-C, R20.Pin_0, R20.Pin_1
  N10: M1.pin_22, M1.pin_23, M1.pin_24, M1.pin_44, R1.Pin_0, R2.Pin_0, R3.Pin_1, R4.Pin_1, R5.Pin_0, R6.Pin_0, R7.Pin_0, R8.Pin_0, R9.Pin_0, R10.Pin_0, R11.Pin_0, R12.Pin_0
  N11: M1.pin_31, D1.I_C
  N12: M1.pin_32, D1.H_C
  N13: M1.pin_33, D1.G_C
  N14: M1.pin_34, D1.F_C
  N15: M1.pin_35, D1.E_C
  N16: M1.pin_36, D1.D_C
  N17: M1.pin_37, D1.C_C
  N18: M1.pin_38, D1.B_C
  N19: M1.pin_39, D1.A_C
  N20: M1.pin_40, S2.Pin_1, S2.Pin_2, R4.Pin_0
  N21: M1.pin_41, S1.Pin_1, S1.Pin_2, R3.Pin_0
  N22: D1.A_A, R12.Pin_1
  N23: D1.B_A, R11.Pin_1
  N24: D1.C_A, R10.Pin_1
  N25: D1.D_A, R9.Pin_1
  N26: D1.E_A, R8.Pin_1
  N27: D1.F_A, R7.Pin_1
  N28: D1.G_A, R6.Pin_1
  N29: D1.H_A, R5.Pin_1
  N30: D1.I_A, R2.Pin_1
  N31: D1.J_A, R1.Pin_1

custom parts:
  ESP32-S2-DevKitC-1: ESP32-S2-DevKitC-1 is an entry-level development board based on ESP32-S2-SOLO (on-board PCB antenna). It is based on the ESP32 microcontroller that boasts Wifi, Bluetooth, Ethernet and Low Power support all in a single chip. (vanepp) Feb 2022: converted to ESP32-S2-DevKitC-1. This module is 44pins long (2x22) and 11 pins width.
